// Logisim project Lucas_Neves_SI4N.circ as structural Verilog: 2 circuits, main circuit main
module main (
  input  in_1,
  input  in_2,
  input  in_3,
  output out_4,
  output out_5
);

  ADD_1 add_1_1 (.A(in_1), .B(in_2), .Vem_1(in_3), .Soma(out_5), .Vai_1(out_4));
endmodule

module ADD_1 (
  input  A,
  input  B,
  input  Vem_1,
  output Soma,
  output Vai_1
);

  wire and_1_out, and_2_out, and_3_out, and_4_out, and_5_out, and_6_out, and_7_out, not_1_out, not_2_out,
       not_3_out, not_4_out, not_5_out, not_6_out;

  not not_1 (not_1_out, A);
  not not_2 (not_2_out, B);
  not not_3 (not_3_out, A);
  not not_4 (not_4_out, Vem_1);
  not not_5 (not_5_out, B);
  not not_6 (not_6_out, Vem_1);
  and and_1 (and_1_out, B, Vem_1);
  and and_2 (and_2_out, A, Vem_1);
  and and_3 (and_3_out, A, B);
  and and_4 (and_4_out, not_1_out, not_2_out, Vem_1);
  and and_5 (and_5_out, not_3_out, B, not_4_out);
  and and_6 (and_6_out, A, not_5_out, not_6_out);
  and and_7 (and_7_out, A, B, Vem_1);
  or or_1 (Vai_1, and_1_out, and_2_out, and_3_out);
  or or_2 (Soma, and_4_out, and_5_out, and_6_out, and_7_out);
endmodule
